# Fritzing sketch single_stepper (saved by Fritzing 0.9.3b)
breadboards: 1

parts:
  M1 = Stepper Motor - Bipolar
  IC1 = L293D [package=THT]
  Raspberry_Pi_1 = Raspberry Pi 3 [part_number=RPI-3-V1.2]
  VCC1 = Battery

nets:
  N1: M1.A, IC1.In_3, IC1.In_4
  N2: M1.C, M1.D, IC1.In_1, IC1.In_2
  N3: IC1.Enable_1, IC1.Enable_2, IC1.+V, Raspberry_Pi_1.5V
  N4: IC1.Out_1_(_Controlled_by_Enable_1_), Raspberry_Pi_1.GIPO18
  N5: IC1.0V, Raspberry_Pi_1.GND, VCC1.-
  N6: IC1.Out_2_(_Controlled_by_Enable_1_), Raspberry_Pi_1.GIPO23
  N7: IC1.+Vmotor, VCC1.+
  N8: IC1.Out_3_(_Controlled_by_Enable_2_), Raspberry_Pi_1.GIPO25
  N9: IC1.Out_4_(_Controlled_by_Enable_2_), Raspberry_Pi_1.GIPO24
